# Fritzing sketch LPG Sensor (saved by Fritzing 0.9.2b)
breadboards: 1

parts:
  DHT1 = DHT11 Humitidy and Temperature Sensor
  7SEG2 = 7-Segment LED I2C Backpack (blue)
  7SEG3 = 7-Segment LED I2C Backpack (blue)
  Part1 = Arduino Micro (Rev3)
  Part2 = Gas Sensor Breakout Board
  LED1 = smd LED [color="Green (555nm)" package="0603 [SMD]"]
  LED2 = smd LED [color="Red (633nm)" package="0603 [SMD]"]
  R1 = Resistor [tolerance=±5% resistance=220 package=THT]
  R2 = Resistor [tolerance=±5% resistance=220 package=THT]
  R3 = Resistor [tolerance=±5% resistance=220 package=THT]

nets:
  VDD: DHT1.VDD, 7SEG2.V+, 7SEG3.V+, Part1.3V3, Part2.A1
  GND: 7SEG2.GND, 7SEG3.GND, Part1.GND, Part2.GND, R1.Pin_0, R2.Pin_0, R3.Pin_1
  N1: 7SEG2.SDA, 7SEG3.SDA, Part1.D2/SDA
  N2: 7SEG2.SCL, 7SEG3.SCL, Part1.D3/SCL
  N3: Part1.D8_PWM/A8, LED2.cathode
  N4: Part1.D9_PWM/A9, LED1.cathode
  N5: Part1.D12_PWM/A11, LED1.anode, R2.Pin_1
  N6: Part1.A0, Part2.B1
  N7: Part2.H1, R3.Pin_0
  N8: LED2.anode, R1.Pin_1

notes:
  Temp (i2c 0x77)
  LPG Value (i2c 0x78)
  Calibrate
  Failure

custom parts:
  DHT11 Humitidy and Temperature Sensor: DHT11 Humidity and Temperature Sensor
  7-Segment LED I2C Backpack (blue): 4-digit, 7-segment LED Display with I2C Control
