# Fritzing sketch Servo-Sweepwith-Matrix (saved by Fritzing 0.9.2b)
breadboards: 1

parts:
  Part1 = Arduino Uno (Rev3)
  LED1 = 8x8 LED Matrix (blue)
  R1 = Resistor [tolerance=±5% resistance=220 package="0805 [SMD]"]
  J1 = Basic Servo
  J2 = Basic Servo

nets:
  N1: Part1.D9_PWM, J1.pulse
  N2: Part1.D10_PWM/SS, J2.pulse
  N3: Part1.A4/SDA, LED1.D
  N4: Part1.A5/SCL, LED1.C
  VCC: Part1.5V, R1.Pin_0, J1.vcc, J2.vcc
  GND: Part1.GND, LED1.-, J1.gnd, J2.gnd
  N5: LED1.+, R1.Pin_1

custom parts:
  8x8 LED Matrix (blue): 8x8 LED Matrix with I2C control (blue)
